// Logisim project ETFStudent.circ as structural Verilog: 9 circuits, main circuit REG32_LD
module REG32_LD (
  input  [31:0] I15__0,
  input  LD,
  input  mr,
  input  CLK,
  output [31:0] A15__0
);

  // REG16_LD reg16_ld_1: pin names not known; wires that end beside it: CLK, mr, I15__0[31:16], A15__0[31:16], LD
  // REG16_LD reg16_ld_2: pin names not known; wires that end beside it: CLK, mr, I15__0[15:0], A15__0[15:0], LD

  // Notes on the sheet:
  //   __
endmodule

module KMADR (
  input  immed,
  input  memdir,
  input  regdir,
  input  memind,
  input  preincr,
  input  postdec,
  input  regindpom,
  output [4:0] Adr4__0
);

  assign Adr4__0 = immed ? 5'b00010 : 5'bz;  // Controlled_Buffer controlled_buffer_1
  assign Adr4__0 = memdir ? 5'b00011 : 5'bz;  // Controlled_Buffer controlled_buffer_2
  assign Adr4__0 = regdir ? 5'b00100 : 5'bz;  // Controlled_Buffer controlled_buffer_3
  assign Adr4__0 = memind ? 5'b00101 : 5'bz;  // Controlled_Buffer controlled_buffer_4
  assign Adr4__0 = preincr ? 5'b01011 : 5'bz;  // Controlled_Buffer controlled_buffer_5
  assign Adr4__0 = postdec ? 5'b01111 : 5'bz;  // Controlled_Buffer controlled_buffer_6
  assign Adr4__0 = regindpom ? 5'b10011 : 5'bz;  // Controlled_Buffer controlled_buffer_7
endmodule

module KMOPR (
  input  HALT,
  input  RTS,
  input  RTI,
  input  ASL,
  input  POPPSW,
  input  PUSH,
  input  POP,
  input  BEQL,
  input  BNEQ,
  input  BLEQU,
  input  BLSS,
  input  JLEQ,
  input  JMP,
  input  JSR,
  input  LD,
  input  ST,
  input  JADR,
  input  TST,
  input  XOR,
  input  STRLEN,
  output [6:0] Adr6__0
);

  assign Adr6__0 = HALT ? 7'b0000010 : 7'bz;  // Controlled_Buffer controlled_buffer_1
  assign Adr6__0 = RTS ? 7'b0000011 : 7'bz;  // Controlled_Buffer controlled_buffer_2
  assign Adr6__0 = RTI ? 7'b0001001 : 7'bz;  // Controlled_Buffer controlled_buffer_3
  assign Adr6__0 = ASL ? 7'b0010100 : 7'bz;  // Controlled_Buffer controlled_buffer_4
  assign Adr6__0 = POPPSW ? 7'b0010101 : 7'bz;  // Controlled_Buffer controlled_buffer_5
  assign Adr6__0 = PUSH ? 7'b0011011 : 7'bz;  // Controlled_Buffer controlled_buffer_6
  assign Adr6__0 = POP ? 7'b0100001 : 7'bz;  // Controlled_Buffer controlled_buffer_7
  assign Adr6__0 = BEQL ? 7'b0101000 : 7'bz;  // Controlled_Buffer controlled_buffer_8
  assign Adr6__0 = BNEQ ? 7'b0101000 : 7'bz;  // Controlled_Buffer controlled_buffer_9
  assign Adr6__0 = BLEQU ? 7'b0101000 : 7'bz;  // Controlled_Buffer controlled_buffer_10
  assign Adr6__0 = BLSS ? 7'b0101000 : 7'bz;  // Controlled_Buffer controlled_buffer_11
  assign Adr6__0 = JLEQ ? 7'b0101010 : 7'bz;  // Controlled_Buffer controlled_buffer_12
  assign Adr6__0 = JMP ? 7'b0101011 : 7'bz;  // Controlled_Buffer controlled_buffer_13
  assign Adr6__0 = JSR ? 7'b0101100 : 7'bz;  // Controlled_Buffer controlled_buffer_14
  assign Adr6__0 = LD ? 7'b0110010 : 7'bz;  // Controlled_Buffer controlled_buffer_15
  assign Adr6__0 = ST ? 7'b0110100 : 7'bz;  // Controlled_Buffer controlled_buffer_16
  assign Adr6__0 = JADR ? 7'b0111011 : 7'bz;  // Controlled_Buffer controlled_buffer_17
  assign Adr6__0 = TST ? 7'b0111100 : 7'bz;  // Controlled_Buffer controlled_buffer_18
  assign Adr6__0 = XOR ? 7'b0111101 : 7'bz;  // Controlled_Buffer controlled_buffer_19
  assign Adr6__0 = STRLEN ? 7'b0111111 : 7'bz;  // Controlled_Buffer controlled_buffer_20
endmodule

module REG6_INC_LD (
  input  [5:0] I5__0,
  input  LD,
  input  INC,
  input  mr,
  input  CLK,
  output [5:0] A5__0
);

  wire reg2m_inc_ld_1_p7, reg2m_inc_ld_2_p8;

  // REG2m_INC_LD reg2m_inc_ld_1: pin names not known; wires that end beside it: CLK, mr, I5__0[5:4], A5__0[5:4], LD, INC, reg2m_inc_ld_1_p7
  // REG2m_INC_LD reg2m_inc_ld_2: pin names not known; wires that end beside it: CLK, reg2m_inc_ld_1_p7, mr, I5__0[3:2], A5__0[3:2], LD, INC, reg2m_inc_ld_2_p8
  // REG2m_INC_LD reg2m_inc_ld_3: pin names not known; wires that end beside it: CLK, reg2m_inc_ld_2_p8, mr, I5__0[1:0], A5__0[1:0], LD, INC, INC

  // Notes on the sheet:
  //   __
endmodule

module ROM_32X20 (
  input  [4:0] ADDR4__0,
  input  CS,
  output [19:0] DOUT
);

  ROM #(.addrWidth(5), .dataWidth(20)) rom_1 (.addr(ADDR4__0), .data(DOUT), .sel(CS));
endmodule

module ROM_32X25 (
  input  [4:0] ADDR4__0,
  input  CS,
  output [24:0] DOUT
);

  ROM #(.addrWidth(5), .dataWidth(25)) rom_1 (.addr(ADDR4__0), .data(DOUT), .sel(CS));
endmodule

module ALU_xor_and_inc_asl___16b (
  input  [15:0] A,
  input  [15:0] B,
  input  INC,
  input  AND,
  input  ASL,
  input  XOR,
  output [15:0] F,
  output Cout
);

  wire adder_1_cout;
  wire [15:0] adder_1_out, and_1_out, xor_1_out;

  Adder #(.width(16)) adder_1 (.a(A), .b(16'h1), .out(adder_1_out), .cin(1'b0), .cout(adder_1_cout));
  assign Cout = INC ? adder_1_cout : 1'bz;  // Controlled_Buffer controlled_buffer_1
  assign Cout = ASL ? A[15] : 1'bz;  // Controlled_Buffer controlled_buffer_2
  assign F = INC ? adder_1_out : 16'bz;  // Controlled_Buffer controlled_buffer_3
  assign F = ASL ? {A[14:0], 1'b0} : 16'bz;  // Controlled_Buffer controlled_buffer_4
  and and_1 (and_1_out[0], A[0], B[0]);
  xor xor_1 (xor_1_out[0], A[0], B[0]);
  and and_2 (and_1_out[1], A[1], B[1]);
  and and_3 (and_1_out[2], A[2], B[2]);
  xor xor_2 (xor_1_out[1], A[1], B[1]);
  xor xor_3 (xor_1_out[2], A[2], B[2]);
  and and_4 (and_1_out[3], A[3], B[3]);
  and and_5 (and_1_out[4], A[4], B[4]);
  xor xor_4 (xor_1_out[4], A[4], B[4]);
  xor xor_5 (xor_1_out[3], A[3], B[3]);
  and and_6 (and_1_out[5], A[5], B[5]);
  and and_7 (and_1_out[6], A[6], B[6]);
  xor xor_6 (xor_1_out[6], A[6], B[6]);
  xor xor_7 (xor_1_out[5], A[5], B[5]);
  and and_8 (and_1_out[7], A[7], B[7]);
  and and_9 (and_1_out[8], A[8], B[8]);
  xor xor_8 (xor_1_out[7], A[7], B[7]);
  xor xor_9 (xor_1_out[8], A[8], B[8]);
  and and_10 (and_1_out[9], A[9], B[9]);
  xor xor_10 (xor_1_out[9], A[9], B[9]);
  and and_11 (and_1_out[10], A[10], B[10]);
  and and_12 (and_1_out[11], A[11], B[11]);
  assign F = AND ? and_1_out : 16'bz;  // Controlled_Buffer controlled_buffer_5
  xor xor_11 (xor_1_out[10], A[10], B[10]);
  xor xor_12 (xor_1_out[11], A[11], B[11]);
  assign F = XOR ? xor_1_out : 16'bz;  // Controlled_Buffer controlled_buffer_6
  and and_13 (and_1_out[12], A[12], B[12]);
  xor xor_13 (xor_1_out[12], A[12], B[12]);
  and and_14 (and_1_out[13], A[13], B[13]);
  xor xor_14 (xor_1_out[13], A[13], B[13]);
  and and_15 (and_1_out[14], A[14], B[14]);
  and and_16 (and_1_out[15], A[15], B[15]);
  xor xor_15 (xor_1_out[14], A[14], B[14]);
  xor xor_16 (xor_1_out[15], A[15], B[15]);

  // Other names for the same wires on the sheet: FOUT[15:0] = F
endmodule

module ROM_128X46 (
  input  [6:0] ADDR6__0,
  input  CS,
  output [31:0] DOUT31__0,
  output [13:0] DOUT45__32
);

  ROM #(.addrWidth(7), .dataWidth(14)) rom_1 (.addr(ADDR6__0), .data(DOUT45__32), .sel(CS));
  ROM #(.addrWidth(7), .dataWidth(32)) rom_2 (.addr(ADDR6__0), .data(DOUT31__0), .sel(CS));
endmodule

module ROM_32X26 (
  input  [4:0] ADDR4__0,
  input  CS,
  output [25:0] DOUT
);

  ROM #(.addrWidth(5), .dataWidth(26)) rom_1 (.addr(ADDR4__0), .data(DOUT), .sel(CS));
endmodule
