// Logisim project ORT2Project.circ as structural Verilog: 8 circuits, main circuit COMPUTER
module COMPUTER (
);

  wire BTN_RST_out, CLK, cpu_1_inta, interrupt_interface_8_1_p4, interrupt_interface_8_1_p5,
       interrupt_interface_8_1_p6, interrupt_interface_8_1_p7, interrupt_interface_8_1_p8,
       interrupt_interface_8_1_p9, interrupt_interface_8_1_p10, interrupt_interface_8_1_p11,
       pull_resistor_4_node, pull_resistor_5_node, ram_1_out_8, rst;
  wire [2:0] cpu_1_uext2__0;
  wire [7:0] interrupt_interface_8_1_p1, pull_resistor_2_node, ram_1_out_7;
  wire [15:0] pull_resistor_1_node;

  Button BTN_RST (.out(BTN_RST_out));
  Clock u_CLK (.out(CLK));
  // RisingEdge risingedge_1: pin names not known; wires that end beside it: BTN_RST_out, CLK, rst
  RAM ram_1 (
    .in_1(pull_resistor_1_node), .in_2(CLK), .in_3(pull_resistor_2_node), .in_4(pull_resistor_4_node),
    .in_5(pull_resistor_5_node), .in_6(rst), .out_7(ram_1_out_7), .out_8(ram_1_out_8));
  Pull_Resistor pull_resistor_1 (.node(pull_resistor_1_node));
  Pull_Resistor pull_resistor_2 (.node(pull_resistor_2_node));
  Pull_Resistor pull_resistor_3 (.node(ram_1_out_7));
  Pull_Resistor pull_resistor_4 (.node(pull_resistor_4_node));
  Pull_Resistor pull_resistor_5 (.node(pull_resistor_5_node));
  Pull_Resistor pull_resistor_6 (.node(ram_1_out_8));
  CPU cpu_1 (
    .in_1(rst), .in_2(CLK), .in_3(ram_1_out_8), .in_4(ram_1_out_7), .ABUS(pull_resistor_1_node),
    .DOUTBUS(pull_resistor_2_node), .out_8(pull_resistor_4_node), .out_9(pull_resistor_5_node),
    .inta(cpu_1_inta), .intr7__0(interrupt_interface_8_1_p1), .UEXT2__0(cpu_1_uext2__0));
  // INTERRUPT_INTERFACE_8 interrupt_interface_8_1: pin names not known; wires that end beside it: interrupt_interface_8_1_p1, cpu_1_inta, cpu_1_uext2__0, interrupt_interface_8_1_p4, interrupt_interface_8_1_p5, interrupt_interface_8_1_p6, interrupt_interface_8_1_p7, interrupt_interface_8_1_p8, interrupt_interface_8_1_p9, interrupt_interface_8_1_p10, interrupt_interface_8_1_p11, CLK
  Button BTN_INTR7 (.out(interrupt_interface_8_1_p4));
  Button BTN_INTR6 (.out(interrupt_interface_8_1_p5));
  Button BTN_INTR5 (.out(interrupt_interface_8_1_p6));
  Button BTN_INTR4 (.out(interrupt_interface_8_1_p7));
  Button BTN_INTR3 (.out(interrupt_interface_8_1_p8));
  Button BTN_INTR2 (.out(interrupt_interface_8_1_p9));
  Button BTN_INTR1 (.out(interrupt_interface_8_1_p10));
  Button BTN_INTR0 (.out(interrupt_interface_8_1_p11));
endmodule

module CPU (
  input  in_1,
  input  in_2,
  input  in_3,
  input  [7:0] in_4,
  input  [7:0] intr7__0,
  output [15:0] ABUS,
  output [7:0] DOUTBUS,
  output out_8,
  output out_9,
  output inta,
  output [2:0] UEXT2__0
);

  wire MDR_ZERO;
  wire [3:0] common_1_phaseffbus;
  wire [6:0] common_1_addrbus, pull_resistor_3_node;
  wire [7:0] pull_resistor_6_node;
  wire [14:0] pull_resistor_5_node;
  wire [15:0] INTRADDR, PSW;
  wire [19:0] common_1_instrucbus;
  wire [20:0] pull_resistor_7_node;

  COMMON common_1 (
    .CLK(in_2), .RST(in_1), .DIN(in_4), .CMEMBUS(pull_resistor_5_node), .MAR(ABUS), .MDR(DOUTBUS),
    .PHASEFFBUS(common_1_phaseffbus), .INSTRUCBUS(common_1_instrucbus), .ADDRBUS(common_1_addrbus),
    .PSW(PSW), .CREGBUS(pull_resistor_7_node), .CFFBUS(pull_resistor_6_node), .MDR_ZERO(MDR_ZERO),
    .CPSW(pull_resistor_3_node), .IVTPPDSP(INTRADDR));
  Pull_Resistor pull_resistor_1 (.node(common_1_instrucbus));
  Pull_Resistor pull_resistor_2 (.node(common_1_phaseffbus));
  Pull_Resistor pull_resistor_3 (.node(pull_resistor_3_node));
  Pull_Resistor pull_resistor_4 (.node(common_1_addrbus));
  Pull_Resistor pull_resistor_5 (.node(pull_resistor_5_node));
  Pull_Resistor pull_resistor_6 (.node(pull_resistor_6_node));
  Pull_Resistor pull_resistor_7 (.node(pull_resistor_7_node));
  FETCH fetch_1 (
    .in_1(in_1), .in_2(in_2), .in_3(in_3), .PHASEFFBUS(common_1_phaseffbus),
    .INSTRUCBUS(common_1_instrucbus), .ADDRBUS(common_1_addrbus), .PSW(PSW), .rdMEM(out_9),
    .CMEMBUS(pull_resistor_5_node), .CFFBUS(pull_resistor_6_node), .CREGBUS(pull_resistor_7_node));
  ADDR addr_1 (
    .in_1(in_1), .in_2(in_2), .in_3(in_3), .PHASEFFBUS(common_1_phaseffbus),
    .INSTRUCBUS(common_1_instrucbus), .ADDRBUS(common_1_addrbus), .rdMEM(out_9),
    .CMEMBUS(pull_resistor_5_node), .CFFBUS(pull_resistor_6_node), .CREGBUS(pull_resistor_7_node));
  EXEC exec_1 (
    .in_1(in_1), .in_2(in_2), .in_3(in_3), .MDR_ZERO(MDR_ZERO), .PHASEFFBUS(common_1_phaseffbus),
    .INSTRUCBUS(common_1_instrucbus), .ADDRBUS(common_1_addrbus), .PSW(PSW), .CMEMBUS(pull_resistor_5_node),
    .CFFBUS(pull_resistor_6_node), .CREGBUS(pull_resistor_7_node), .CPSW(pull_resistor_3_node),
    .rdMEM(out_9), .wrMEM(out_8));
  INTR intr_1 (
    .in_1(in_1), .in_2(in_2), .in_3(in_3), .PHASEFFBUS(common_1_phaseffbus),
    .INSTRUCBUS(common_1_instrucbus), .PSW(PSW), .intr(intr7__0), .ADDIVTP(INTRADDR),
    .CMEMBUS(pull_resistor_5_node), .CFFBUS(pull_resistor_6_node), .CREGBUS(pull_resistor_7_node),
    .rdMEM(out_9), .wrMEM(out_8), .UEXT__0(UEXT2__0), .inta(inta));

  // Other names for the same wires on the sheet: CLK = in_2; DIN7__0[7:0] = in_4; FCBUS = in_3; MAR[15:0] = ABUS;
  //   MDR[7:0] = DOUTBUS; RD = out_9; rst = in_1; WR = out_8
endmodule

module COMMON (
  input  CLK,
  input  RST,
  input  [7:0] DIN,
  input  [15:0] IVTPPDSP,
  input  [14:0] CMEMBUS,
  input  [7:0] CFFBUS,
  input  [20:0] CREGBUS,
  input  [6:0] CPSW,
  output [15:0] MAR,
  output [7:0] MDR,
  output [3:0] PHASEFFBUS,
  output [19:0] INSTRUCBUS,
  output [6:0] ADDRBUS,
  output [15:0] PSW,
  output MDR_ZERO
);

  wire add16_1_p1, add16_2_p1, adr_inst, and_13_out, and_14_out, and_15_out, and_16_out, and_17_out,
       and_18_out, and_19_out, and_20_out, and_21_out, and_22_out, and_23_out, and_24_out, and_25_out,
       and_26_out, and_27_out, and_28_out, and_29_out, and_30_out, and_31_out, and_32_out, and_33_out,
       and_34_out, and_35_out, and_36_out, bezadr_inst, branch_inst, Cout, jump_inst, mp2_16b_1_p3,
       mp2_16b_2_p3, mp4_16b_1_p7, mp4_16b_2_p5, mp4_16b_2_p8, mp4_16b_3_p5, mp8_8b_1_p8, mp8_16b_1_p8,
       not_1_out, not_2_out, not_6_out, not_9_out, or_1_out, or_3_out, or_4_out, or_5_out, or_6_out,
       or_7_out, or_8_out, or_9_out, or_10_out, or_11_out, or_12_out, or_13_out, or_14_out, or_15_out,
       or_16_out, or_17_out, or_18_out, reg16_inc_ld_2_p4, reg16_ld_1_p3, rsff_2_p4, rsff_3_p4, rsff_4_p4,
       rsff_6_p4, rsff_7_p4, rsff_9_p4, rsff_10_p4;
  wire [2:0] IR26__24;
  wire [7:0] IR7__0, IR15__8, IR23__16;
  wire [7:3] IR31__24;
  wire [15:0] A15__0, ADD_PCRELPOM, ADD_REGINDPOM, ALU15__0, B15__0, DW, GPR15__0, PC15__0, SP15__0;

  // MP8_16b mp8_16b_1: pin names not known; wires that end beside it: CMEMBUS[7], CMEMBUS[6], CMEMBUS[5], PC15__0, {IR7__0, IR15__8}, GPR15__0, DW, mp8_16b_1_p8, B15__0, ADD_REGINDPOM, SP15__0, IVTPPDSP, 1'b1
  // REG16_INC_LD reg16_inc_ld_1: pin names not known; wires that end beside it: CLK, mp8_16b_1_p8, MAR, CMEMBUS[0], CMEMBUS[1]
  // REG8_LD reg8_ld_1: pin names not known; wires that end beside it: CLK, MDR, {IR31__24, IR26__24}, CREGBUS[14]
  // REG8_LD reg8_ld_2: pin names not known; wires that end beside it: CLK, MDR, IR15__8, CREGBUS[12]
  and and_1 (bezadr_inst, ~IR31__24[3], ~IR31__24[4], ~IR31__24[5], ~IR31__24[6], ~IR31__24[7], PSW[0]);  // AND_Gate
  and and_2 (branch_inst, ~IR31__24[3], IR31__24[4], ~IR31__24[5], ~IR31__24[6], ~IR31__24[7], PSW[0]);  // AND_Gate
  and and_3 (adr_inst, ~IR31__24[3], IR31__24[4], IR31__24[5], ~IR31__24[6], ~IR31__24[7], PSW[0]);  // AND_Gate
  and and_4 (jump_inst, ~IR26__24[1], ~IR26__24[2], ~IR31__24[3], ~IR31__24[4], IR31__24[5], ~IR31__24[6], ~IR31__24[7], PSW[0]);  // AND_Gate
  // ADD16 add16_1: pin names not known; wires that end beside it: add16_1_p1, add16_1_p1, {{9{IR15__8[7]}}, IR15__8[6:0]}, ADD_REGINDPOM, GPR15__0
  or or_1 (or_1_out, RST, CREGBUS[15]);
  not not_1 (not_1_out, or_1_out);
  // REG16_LD reg16_ld_1: pin names not known; wires that end beside it: CLK, not_1_out, reg16_ld_1_p3, A15__0, CREGBUS[8]
  and and_5 (ADDRBUS[0], ~IR23__16[0], ~IR23__16[1], ~IR23__16[2], ~IR23__16[3], ~IR23__16[4], ~IR23__16[5], ~IR23__16[6], ~IR23__16[7], adr_inst);  // AND_Gate
  and and_6 (ADDRBUS[1], ~IR23__16[0], ~IR23__16[1], ~IR23__16[2], ~IR23__16[3], IR23__16[4], ~IR23__16[5], ~IR23__16[6], ~IR23__16[7], adr_inst);  // AND_Gate
  and and_7 (ADDRBUS[2], ~IR23__16[0], ~IR23__16[1], ~IR23__16[2], ~IR23__16[3], IR23__16[4], IR23__16[5], ~IR23__16[6], ~IR23__16[7], adr_inst);  // AND_Gate
  // MP4_16b mp4_16b_1: pin names not known; wires that end beside it: CREGBUS[10], CREGBUS[9], DW, ALU15__0, reg16_ld_1_p3, B15__0, mp4_16b_1_p7, 1'b1, mp4_16b_1_p7
  // REG8_LD reg8_ld_3: pin names not known; wires that end beside it: CLK, MDR, IR23__16, CREGBUS[13]
  // REG8_LD reg8_ld_4: pin names not known; wires that end beside it: CLK, MDR, IR7__0, CREGBUS[11]
  // DC3_8 dc3_8_1: pin names not known; wires that end beside it: IR26__24, bezadr_inst, INSTRUCBUS[0], INSTRUCBUS[1], INSTRUCBUS[2], INSTRUCBUS[3], INSTRUCBUS[4], INSTRUCBUS[5], INSTRUCBUS[6]
  // DC1_2 dc1_2_1: pin names not known; wires that end beside it: IR26__24[0], jump_inst, INSTRUCBUS[18], INSTRUCBUS[19]
  // MP8_8b mp8_8b_1: pin names not known; wires that end beside it: CMEMBUS[12], CMEMBUS[13], CMEMBUS[14], DIN, A15__0[15:8], A15__0[7:0], PC15__0[15:8], mp8_8b_1_p8, PC15__0[7:0], {PSW[15], {7{1'b0}}}, {3'b000, PSW[4:0]}, 1'b1
  // REG8_LD reg8_ld_5: pin names not known; wires that end beside it: CLK, mp8_8b_1_p8, MDR, CMEMBUS[2]
  // MP4_16b mp4_16b_2: pin names not known; wires that end beside it: CREGBUS[0], CREGBUS[1], {IR7__0, IR15__8}, GPR15__0, mp4_16b_2_p5, mp4_16b_2_p5, DW, mp4_16b_2_p8, 1'b1, mp4_16b_2_p8
  // REG16 reg16_1: pin names not known; wires that end beside it: CLK, B15__0, CREGBUS[2], CREGBUS[3], CREGBUS[4]
  // ADD16 add16_2: pin names not known; wires that end beside it: add16_2_p1, add16_2_p1, {{9{IR23__16[7]}}, IR23__16[6:0]}, ADD_PCRELPOM, PC15__0
  and and_8 (ADDRBUS[3], ~IR23__16[4], IR23__16[5], ~IR23__16[6], ~IR23__16[7], adr_inst);  // AND_Gate
  and and_9 (ADDRBUS[4], ~IR23__16[4], ~IR23__16[5], IR23__16[6], ~IR23__16[7], adr_inst);  // AND_Gate
  and and_10 (ADDRBUS[5], IR23__16[4], ~IR23__16[5], IR23__16[6], ~IR23__16[7], adr_inst);  // AND_Gate
  and and_11 (ADDRBUS[6], ~IR23__16[4], IR23__16[5], IR23__16[6], ~IR23__16[7], adr_inst);  // AND_Gate
  // DC3_8 dc3_8_2: pin names not known; wires that end beside it: IR26__24, branch_inst, INSTRUCBUS[7], INSTRUCBUS[8], INSTRUCBUS[9], INSTRUCBUS[10], INSTRUCBUS[11]
  and and_12 (MDR_ZERO, ~MDR[0], ~MDR[1], ~MDR[2], ~MDR[3], ~MDR[4], ~MDR[5], ~MDR[6], ~MDR[7]);  // AND_Gate
  // MP4_16b mp4_16b_3: pin names not known; wires that end beside it: CMEMBUS[11], CMEMBUS[10], DW, ADD_PCRELPOM, mp4_16b_3_p5, {IR15__8, IR23__16}, MAR, 1'b1
  // REG8_LD reg8_ld_6: pin names not known; wires that end beside it: CLK, MDR, DW[15:8], CREGBUS[6]
  not not_2 (not_2_out, RST);
  // RSFF rsff_1: pin names not known; wires that end beside it: CFFBUS[1], CLK, CFFBUS[0], not_2_out, PHASEFFBUS[0]
  // MP2_16b mp2_16b_1: pin names not known; wires that end beside it: RST, mp4_16b_3_p5, mp2_16b_1_p3, 16'h1000, 1'b1
  // REG16_INC_LD reg16_inc_ld_2: pin names not known; wires that end beside it: CLK, mp2_16b_1_p3, PC15__0, reg16_inc_ld_2_p4, CMEMBUS[4]
  // DC3_8 dc3_8_3: pin names not known; wires that end beside it: IR26__24, adr_inst, INSTRUCBUS[17], INSTRUCBUS[12], INSTRUCBUS[13], INSTRUCBUS[14], INSTRUCBUS[15], INSTRUCBUS[16]
  // MP2_16b mp2_16b_2: pin names not known; wires that end beside it: CREGBUS[16], B15__0, mp2_16b_2_p3, mp2_16b_2_p3, A15__0, 1'b1
  // GPR8x16 gpr8x16_1: pin names not known; wires that end beside it: IR23__16[3:1], CLK, GPR15__0, CREGBUS[5]
  or or_2 (reg16_inc_ld_2_p4, CMEMBUS[3], RST);
  // REG8_LD reg8_ld_7: pin names not known; wires that end beside it: CLK, MDR, DW[7:0], CREGBUS[7]
  // RSFF rsff_2: pin names not known; wires that end beside it: CFFBUS[3], CLK, CFFBUS[2], rsff_2_p4, PHASEFFBUS[1]
  not not_3 (rsff_2_p4, RST);
  // REG16 reg16_2: pin names not known; wires that end beside it: CLK, 16'hf000, SP15__0, RST, CMEMBUS[8], CMEMBUS[9]
  or or_3 (or_3_out, INSTRUCBUS[2], INSTRUCBUS[4]);
  or or_4 (or_4_out, INSTRUCBUS[2], INSTRUCBUS[4]);
  or or_5 (or_5_out, INSTRUCBUS[12], INSTRUCBUS[16], INSTRUCBUS[17], INSTRUCBUS[6]);
  or or_6 (or_6_out, INSTRUCBUS[15], INSTRUCBUS[3]);
  or or_7 (or_7_out, INSTRUCBUS[12], INSTRUCBUS[16], INSTRUCBUS[17], INSTRUCBUS[6]);
  and and_13 (and_13_out, or_7_out, A15__0[15]);
  or or_8 (or_8_out, INSTRUCBUS[2], INSTRUCBUS[4]);
  or or_9 (or_9_out, INSTRUCBUS[17], INSTRUCBUS[3]);
  or or_10 (or_10_out, INSTRUCBUS[2], INSTRUCBUS[4]);
  or or_11 (or_11_out, INSTRUCBUS[2], INSTRUCBUS[4]);
  // RSFF rsff_3: pin names not known; wires that end beside it: CFFBUS[5], CLK, CFFBUS[4], rsff_3_p4, PHASEFFBUS[2]
  not not_4 (rsff_3_p4, RST);
  and and_14 (and_14_out, CPSW[1], ~DW[0], or_3_out);  // AND_Gate
  and and_15 (and_15_out, CPSW[1], DW[0], or_3_out);
  and and_16 (and_16_out, DW[1], or_4_out);
  and and_17 (and_17_out, ~A15__0[0], ~A15__0[1], ~A15__0[2], ~A15__0[3], ~A15__0[4], ~A15__0[5], ~A15__0[6], ~A15__0[7], ~A15__0[8], ~A15__0[9], ~A15__0[10], ~A15__0[11], ~A15__0[12], ~A15__0[13], ~A15__0[14], ~A15__0[15]);  // AND_Gate
  and and_18 (and_18_out, ~ALU15__0[0], ~ALU15__0[1], ~ALU15__0[2], ~ALU15__0[3], ~ALU15__0[4], ~ALU15__0[5], ~ALU15__0[6], ~ALU15__0[7], ~ALU15__0[8], ~ALU15__0[9], ~ALU15__0[10], ~ALU15__0[11], ~ALU15__0[12], ~ALU15__0[13], ~ALU15__0[14], ~ALU15__0[15]);  // AND_Gate
  and and_19 (and_19_out, DW[4], or_8_out);
  and and_20 (and_20_out, or_9_out, Cout);
  and and_21 (and_21_out, DW[3], or_10_out);
  and and_22 (and_22_out, INSTRUCBUS[17], A15__0[15]);
  and and_23 (and_23_out, CPSW[6], ~DW[15], or_11_out);  // AND_Gate
  and and_24 (and_24_out, CPSW[6], DW[15], or_11_out);
  or or_12 (or_12_out, and_16_out, and_25_out, and_26_out);
  and and_25 (and_25_out, or_5_out, and_17_out);
  and and_26 (and_26_out, or_6_out, and_18_out);
  and and_27 (and_27_out, DW[2], or_13_out);
  or or_13 (or_13_out, INSTRUCBUS[2], INSTRUCBUS[4]);
  or or_14 (or_14_out, INSTRUCBUS[15], INSTRUCBUS[3]);
  and and_28 (and_28_out, or_14_out, ALU15__0[15]);
  or or_15 (or_15_out, and_19_out, and_20_out);
  or or_16 (or_16_out, and_21_out, and_22_out);
  or or_17 (or_17_out, CPSW[0], and_14_out);
  and and_29 (and_29_out, CPSW[2], ~or_12_out);  // AND_Gate
  and and_30 (and_30_out, CPSW[2], or_12_out);
  or or_18 (or_18_out, and_27_out, and_13_out, and_28_out);
  and and_31 (and_31_out, CPSW[4], ~or_15_out);  // AND_Gate
  and and_32 (and_32_out, CPSW[4], or_15_out);
  and and_33 (and_33_out, CPSW[5], ~or_16_out);  // AND_Gate
  and and_34 (and_34_out, CPSW[5], or_16_out);
  // RSFF rsff_4: pin names not known; wires that end beside it: CFFBUS[7], CLK, CFFBUS[6], rsff_4_p4, PHASEFFBUS[3], ALU15__0, Cout, A15__0
  not not_5 (rsff_4_p4, RST);
  not not_6 (not_6_out, RST);
  // RSFF rsff_5: pin names not known; wires that end beside it: or_17_out, CLK, and_15_out, not_6_out, PSW[0]
  and and_35 (and_35_out, CPSW[3], ~or_18_out);  // AND_Gate
  and and_36 (and_36_out, CPSW[3], or_18_out);
  // RSFF rsff_6: pin names not known; wires that end beside it: and_31_out, CLK, and_32_out, rsff_6_p4, PSW[4]
  not not_7 (rsff_6_p4, RST);
  // RSFF rsff_7: pin names not known; wires that end beside it: and_33_out, CLK, and_34_out, rsff_7_p4, PSW[3]
  not not_8 (rsff_7_p4, RST);
  not not_9 (not_9_out, RST);
  // RSFF rsff_8: pin names not known; wires that end beside it: and_23_out, CLK, and_24_out, not_9_out, PSW[15]
  ALU_xor_and_inc_asl___16b alu_xor_and_inc_asl_16b_1 (
    .A(A15__0), .B(B15__0), .INC(CREGBUS[17]), .AND(CREGBUS[19]), .ASL(CREGBUS[18]), .XOR(CREGBUS[20]),
    .F(ALU15__0), .Cout(Cout));
  // RSFF rsff_9: pin names not known; wires that end beside it: and_29_out, CLK, and_30_out, rsff_9_p4, PSW[1]
  not not_10 (rsff_9_p4, RST);
  // RSFF rsff_10: pin names not known; wires that end beside it: and_35_out, CLK, and_36_out, rsff_10_p4, PSW[2]
  not not_11 (rsff_10_p4, RST);

  assign PSW[14:5] = {10{1'b0}};

  // Other names for the same wires on the sheet: immed = ADDRBUS[0]; memdir = ADDRBUS[1]; memind = ADDRBUS[2];
  //   regdir = ADDRBUS[3]; preincr = ADDRBUS[4]; postdec = ADDRBUS[5]; regindpom = ADDRBUS[6]; stFETCH = CFFBUS[0];
  //   clFETCH = CFFBUS[1]; stADDR = CFFBUS[2]; clADDR = CFFBUS[3]; stEXEC = CFFBUS[4]; clEXEC = CFFBUS[5];
  //   stINTR = CFFBUS[6]; clINTR = CFFBUS[7]; ldMAR = CMEMBUS[0]; incMAR = CMEMBUS[1]; ldMDR = CMEMBUS[2];
  //   ldPC = CMEMBUS[3]; incPC = CMEMBUS[4]; mxMAR0 = CMEMBUS[5]; mxMAR1 = CMEMBUS[6]; mxMAR2 = CMEMBUS[7];
  //   incSP = CMEMBUS[8]; decSP = CMEMBUS[9]; mxPC0 = CMEMBUS[10]; mxPC1 = CMEMBUS[11]; mxMDR2 = CMEMBUS[12];
  //   mxMDR1 = CMEMBUS[13]; mxMDR0 = CMEMBUS[14]; clPSWSTART = CPSW[0]; ldST = CPSW[1]; ldZ = CPSW[2]; ldN = CPSW[3];
  //   ldC = CPSW[4]; ldV = CPSW[5]; ldI = CPSW[6]; mxB1 = CREGBUS[0]; mxB0 = CREGBUS[1]; ldB = CREGBUS[2];
  //   incB = CREGBUS[3]; decB = CREGBUS[4]; wrGPR = CREGBUS[5]; ldDWH = CREGBUS[6]; ldDWL = CREGBUS[7];
  //   ldA = CREGBUS[8]; mxA0 = CREGBUS[9]; mxA1 = CREGBUS[10]; ldIR7__0 = CREGBUS[11]; ldIR15__8 = CREGBUS[12];
  //   ldIR23__16 = CREGBUS[13]; ldIR31__24 = CREGBUS[14]; clA = CREGBUS[15]; mxGPR0 = CREGBUS[16];
  //   incALU = CREGBUS[17]; aslALU = CREGBUS[18]; andALU = CREGBUS[19]; xorALU = CREGBUS[20]; Din7__0[7:0] = DIN;
  //   ENTRADDR15__0[15:0] = IVTPPDSP; HALT = INSTRUCBUS[0]; RTS = INSTRUCBUS[1]; RTI = INSTRUCBUS[2];
  //   ASL = INSTRUCBUS[3]; POPPSW = INSTRUCBUS[4]; PUSH = INSTRUCBUS[5]; POP = INSTRUCBUS[6]; BEQL = INSTRUCBUS[7];
  //   BNEQ = INSTRUCBUS[8]; BLEQU = INSTRUCBUS[9]; BLSS = INSTRUCBUS[10]; JLEQ = INSTRUCBUS[11]; LD = INSTRUCBUS[12];
  //   ST = INSTRUCBUS[13]; JADR = INSTRUCBUS[14]; TST = INSTRUCBUS[15]; XOR = INSTRUCBUS[16]; STRLEN = INSTRUCBUS[17];
  //   JMP = INSTRUCBUS[18]; JSR = INSTRUCBUS[19]; IR31__24[2:0] = IR26__24; IR31__27[4:0] = IR31__24;
  //   MAR15__0[15:0] = MAR; MDR7__0[7:0] = MDR; FETCH = PHASEFFBUS[0]; ADDR = PHASEFFBUS[1]; EXEC = PHASEFFBUS[2];
  //   INTR = PHASEFFBUS[3]; PSW15__0 (some bits) = {PSW[15], PSW[4:0]}; PSWSTART = PSW[0]; PSWZ = PSW[1];
  //   PSWN = PSW[2]; PSWV = PSW[3]; PSWC = PSW[4]; PSWI = PSW[15]

  // Notes on the sheet:
  //   Instrukcijski registar
  //   SABIRAC - GPR + POM
  //   MAR
  //   Prepoznavanje nacina adresiranja
  //   PRIHVATNI REGISTAR PODATAKA - B
  //   AKUMULATOR
  //   Dekoderi za prepoznavanje instrukcije na osnovu sadrzaja registra IR31..24
  //   MDR
  //   SABIRAC - PC + POM
  //   LOGICKI SIGNAL - MDR_ZERO
  //   REGISTARSKI FAJL - GPR
  //   POMOCNI REGISTAR - DW
  //   FF za pokretanje FETCH, ADDR, EXEC i INTR faze izvršavanja instrukcije
  //   PC
  //   POKAZIVAC NA VRH STEKA - SP
  //   A
  //   15
  //   A
  //   15
  //   ALU
  //   Programska statusna reč (PSW)
  //   15
  //   ALU
endmodule

module FETCH (
  input  in_1,
  input  in_2,
  input  in_3,
  input  [3:0] PHASEFFBUS,
  input  [19:0] INSTRUCBUS,
  input  [6:0] ADDRBUS,
  input  [15:0] PSW,
  output [14:0] CMEMBUS,
  output [7:0] CFFBUS,
  output [20:0] CREGBUS,
  output rdMEM
);

  wire ADR, adr2, adr3, adr4, and_5_out, and_6_out, and_7_out, and_8_out, and_9_out, and_10_out, and_11_out,
       and_12_out, and_13_out, and_14_out, and_15_out, and_16_out, bezadr1, bradr2, bradr3, brbezadr1, brcnd,
       brgradr, brgrinst, brjump2, brjump3, brnotFCBUS, brnotPSWSTandFETCH, bruncd, clFETCH, gradr, grinst,
       incPC, jump2, jump3, ldIR7__0, ldIR15__8, ldIR23__16, ldIR31__24, ldMAR, ldMDR, not_1_out, not_3_out,
       not_4_out, or_5_out, or_7_out, or_8_out, or_9_out, PSWSTandFETCH, rdMEM_t, reg8_inc_ld_1_p5,
       reg8_inc_ld_1_p6, stADDR, stEXEC;
  wire [2:0] reg8_inc_ld_1_p3_2;
  wire [7:0] reg8_inc_ld_1_p4;
  wire [19:11] reg8_inc_ld_1_p3;

  or or_1 (ADR, INSTRUCBUS[12], INSTRUCBUS[13], INSTRUCBUS[14], INSTRUCBUS[15], INSTRUCBUS[16], INSTRUCBUS[17]);
  or or_2 (bezadr1, INSTRUCBUS[0], INSTRUCBUS[1], INSTRUCBUS[2], INSTRUCBUS[3], INSTRUCBUS[4], INSTRUCBUS[5], INSTRUCBUS[6]);
  or or_3 (jump2, INSTRUCBUS[7], INSTRUCBUS[8], INSTRUCBUS[9], INSTRUCBUS[10]);
  or or_4 (jump3, INSTRUCBUS[11], INSTRUCBUS[18], INSTRUCBUS[19]);
  or or_5 (or_5_out, ADDRBUS[3], ADDRBUS[4], ADDRBUS[5]);
  not not_1 (not_1_out, in_1);
  // REG8_INC_LD reg8_inc_ld_1: pin names not known; wires that end beside it: in_2, not_1_out, {reg8_inc_ld_1_p3_2, reg8_inc_ld_1_p3[19:15]}, reg8_inc_ld_1_p4, reg8_inc_ld_1_p5, reg8_inc_ld_1_p6
  and and_1 (adr2, ADR, or_5_out);
  and and_2 (adr3, ADR, ADDRBUS[6]);
  not not_2 (reg8_inc_ld_1_p6, reg8_inc_ld_1_p5);
  or or_6 (reg8_inc_ld_1_p5, bruncd, brcnd);
  ROM_32X20 rom_32x20_1 (
    .ADDR4__0(reg8_inc_ld_1_p4[4:0]), .CS(1'b1),
    .DOUT({reg8_inc_ld_1_p3, stEXEC, stADDR, clFETCH, ldIR7__0, ldIR15__8, ldIR23__16, ldIR31__24, ldMDR, rdMEM_t, incPC, ldMAR}));
  or or_7 (or_7_out, ADDRBUS[0], ADDRBUS[1], ADDRBUS[2]);
  and and_3 (adr4, ADR, or_7_out);
  // DC4_16 dc4_16_1: pin names not known; wires that end beside it: reg8_inc_ld_1_p3[14:11], bruncd, brnotPSWSTandFETCH, brnotFCBUS, brgrinst, brbezadr1, brgradr, brjump2, bradr2, brjump3, bradr3
  or or_8 (or_8_out, INSTRUCBUS[14], INSTRUCBUS[17]);
  or or_9 (or_9_out, ADDRBUS[0], ADDRBUS[3]);
  and and_4 (grinst, ~ADR, ~bezadr1, ~jump2, ~jump3);  // AND_Gate
  and and_5 (and_5_out, ~adr4, ~adr3, ~adr2, ADR);  // AND_Gate
  and and_6 (and_6_out, INSTRUCBUS[13], ADDRBUS[0]);
  and and_7 (and_7_out, or_8_out, or_9_out);
  or or_10 (gradr, and_5_out, and_6_out, and_7_out);
  not not_3 (not_3_out, PSWSTandFETCH);
  not not_4 (not_4_out, in_3);
  and and_8 (and_8_out, not_3_out, brnotPSWSTandFETCH);
  and and_9 (and_9_out, not_4_out, brnotFCBUS);
  and and_10 (and_10_out, grinst, brgrinst);
  and and_11 (and_11_out, bezadr1, brbezadr1);
  and and_12 (and_12_out, gradr, brgradr);
  and and_13 (and_13_out, jump2, brjump2);
  and and_14 (and_14_out, adr2, bradr2);
  and and_15 (and_15_out, jump3, brjump3);
  and and_16 (and_16_out, adr3, bradr3);
  and and_17 (PSWSTandFETCH, PHASEFFBUS[0], PSW[0]);
  or or_11 (brcnd, and_8_out, and_9_out, and_10_out, and_11_out, and_12_out, and_13_out, and_14_out, and_15_out, and_16_out);
  assign CMEMBUS[0] = ldMAR ? 1'b1 : 1'bz;  // Controlled_Buffer controlled_buffer_1
  assign CMEMBUS[2] = ldMDR ? 1'b1 : 1'bz;  // Controlled_Buffer controlled_buffer_2
  assign CMEMBUS[4] = incPC ? 1'b1 : 1'bz;  // Controlled_Buffer controlled_buffer_3
  assign CFFBUS[1] = clFETCH ? 1'b1 : 1'bz;  // Controlled_Buffer controlled_buffer_4
  assign CFFBUS[2] = stADDR ? 1'b1 : 1'bz;  // Controlled_Buffer controlled_buffer_5
  assign CFFBUS[4] = stEXEC ? 1'b1 : 1'bz;  // Controlled_Buffer controlled_buffer_6
  assign CREGBUS[11] = ldIR7__0 ? 1'b1 : 1'bz;  // Controlled_Buffer controlled_buffer_7
  assign CREGBUS[12] = ldIR15__8 ? 1'b1 : 1'bz;  // Controlled_Buffer controlled_buffer_8
  assign CREGBUS[13] = ldIR23__16 ? 1'b1 : 1'bz;  // Controlled_Buffer controlled_buffer_9
  assign CREGBUS[14] = ldIR31__24 ? 1'b1 : 1'bz;  // Controlled_Buffer controlled_buffer_10
  assign rdMEM = rdMEM_t ? 1'b1 : 1'bz;  // Controlled_Buffer controlled_buffer_11

  // Other names for the same wires on the sheet: immed = ADDRBUS[0]; memdir = ADDRBUS[1]; memind = ADDRBUS[2];
  //   regdir = ADDRBUS[3]; preincr = ADDRBUS[4]; postdec = ADDRBUS[5]; regindpom = ADDRBUS[6]; CLK = in_2;
  //   FCBUS = in_3; HALT = INSTRUCBUS[0]; RTS = INSTRUCBUS[1]; RTI = INSTRUCBUS[2]; ASL = INSTRUCBUS[3];
  //   POPPSW = INSTRUCBUS[4]; PUSH = INSTRUCBUS[5]; POP = INSTRUCBUS[6]; BEQL = INSTRUCBUS[7]; BNEQ = INSTRUCBUS[8];
  //   BLEQU = INSTRUCBUS[9]; BLSS = INSTRUCBUS[10]; JLEQ = INSTRUCBUS[11]; LD = INSTRUCBUS[12]; ST = INSTRUCBUS[13];
  //   JADR = INSTRUCBUS[14]; TST = INSTRUCBUS[15]; XOR = INSTRUCBUS[16]; STRLEN = INSTRUCBUS[17];
  //   JMP = INSTRUCBUS[18]; JSR = INSTRUCBUS[19]; FETCH = PHASEFFBUS[0]; PSWSTART = PSW[0]; rst = in_1

  // Notes on the sheet:
  //   Operaciona jedinica
  //   Kontrolna jedinica
endmodule

module ADDR (
  input  in_1,
  input  in_2,
  input  in_3,
  input  [3:0] PHASEFFBUS,
  input  [19:0] INSTRUCBUS,
  input  [6:0] ADDRBUS,
  output [14:0] CMEMBUS,
  output [7:0] CFFBUS,
  output [20:0] CREGBUS,
  output rdMEM
);

  wire and_1_out, and_2_out, and_3_out, bradr, brcnd, brNoRead, brnotADDR, brnotFCBUS, bruncnd, clADDR, decB,
       incB, incMAR, ldB, ldDWH, ldDWL, ldMAR, ldMDR, mp2_8b_1_p3, mxB0, mxB1, mxMAR0, mxMAR1, mxMAR2,
       not_1_out, or_2_out, rdMEM_t, reg8_inc_ld_1_p5, reg8_inc_ld_1_p6, stEXEC, wrGPR;
  wire [2:0] reg8_inc_ld_1_p4_2;
  wire [4:0] mp2_8b_1_p4, reg8_inc_ld_1_p4;
  wire [24:17] dc3_8_1_p7;

  not not_1 (not_1_out, in_1);
  // MP2_8b mp2_8b_1: pin names not known; wires that end beside it: bradr, {3'b000, dc3_8_1_p7[24:20]}, mp2_8b_1_p3, {3'b000, mp2_8b_1_p4}, 1'b1
  // REG8_INC_LD reg8_inc_ld_1: pin names not known; wires that end beside it: in_2, not_1_out, mp2_8b_1_p3, {reg8_inc_ld_1_p4_2, reg8_inc_ld_1_p4}, reg8_inc_ld_1_p5, reg8_inc_ld_1_p6
  // DC3_8 dc3_8_1: pin names not known; wires that end beside it: bradr, brNoRead, brnotFCBUS, brnotADDR, bruncnd, 1'b1, dc3_8_1_p7[19:17]
  not not_2 (reg8_inc_ld_1_p6, reg8_inc_ld_1_p5);
  or or_1 (reg8_inc_ld_1_p5, bradr, bruncnd, brcnd);
  ROM_32X25 rom_32x25_1 (
    .ADDR4__0(reg8_inc_ld_1_p4), .CS(1'b1),
    .DOUT({dc3_8_1_p7, stEXEC, clADDR, mxB1, decB, wrGPR, mxMAR2, incB, mxMAR1, ldDWH, incMAR, ldDWL, ldMDR, rdMEM_t, mxB0, ldMAR, mxMAR0, ldB}));
  KMADR kmadr_1 (
    .immed(ADDRBUS[0]), .memdir(ADDRBUS[1]), .regdir(ADDRBUS[3]), .memind(ADDRBUS[2]), .Adr4__0(mp2_8b_1_p4),
    .preincr(ADDRBUS[4]), .postdec(ADDRBUS[5]), .regindpom(ADDRBUS[6]));
  and and_1 (and_1_out, brNoRead, or_2_out);
  or or_2 (or_2_out, INSTRUCBUS[13], INSTRUCBUS[14], INSTRUCBUS[17]);
  and and_2 (and_2_out, brnotFCBUS, ~in_3);  // AND_Gate
  and and_3 (and_3_out, brnotADDR, ~PHASEFFBUS[1]);  // AND_Gate
  or or_3 (brcnd, and_1_out, and_2_out, and_3_out);
  assign CMEMBUS[0] = ldMAR ? 1'b1 : 1'bz;  // Controlled_Buffer controlled_buffer_1
  assign CMEMBUS[1] = incMAR ? 1'b1 : 1'bz;  // Controlled_Buffer controlled_buffer_2
  assign CMEMBUS[2] = ldMDR ? 1'b1 : 1'bz;  // Controlled_Buffer controlled_buffer_3
  assign CREGBUS[0] = mxB1 ? 1'b1 : 1'bz;  // Controlled_Buffer controlled_buffer_4
  assign CREGBUS[1] = mxB0 ? 1'b1 : 1'bz;  // Controlled_Buffer controlled_buffer_5
  assign CREGBUS[2] = ldB ? 1'b1 : 1'bz;  // Controlled_Buffer controlled_buffer_6
  assign CREGBUS[3] = incB ? 1'b1 : 1'bz;  // Controlled_Buffer controlled_buffer_7
  assign CREGBUS[4] = decB ? 1'b1 : 1'bz;  // Controlled_Buffer controlled_buffer_8
  assign CREGBUS[5] = wrGPR ? 1'b1 : 1'bz;  // Controlled_Buffer controlled_buffer_9
  assign CREGBUS[6] = ldDWH ? 1'b1 : 1'bz;  // Controlled_Buffer controlled_buffer_10
  assign CREGBUS[7] = ldDWL ? 1'b1 : 1'bz;  // Controlled_Buffer controlled_buffer_11
  assign CMEMBUS[5] = mxMAR0 ? 1'b1 : 1'bz;  // Controlled_Buffer controlled_buffer_12
  assign CMEMBUS[6] = mxMAR1 ? 1'b1 : 1'bz;  // Controlled_Buffer controlled_buffer_13
  assign CMEMBUS[7] = mxMAR2 ? 1'b1 : 1'bz;  // Controlled_Buffer controlled_buffer_14
  assign CFFBUS[3] = clADDR ? 1'b1 : 1'bz;  // Controlled_Buffer controlled_buffer_15
  assign CFFBUS[4] = stEXEC ? 1'b1 : 1'bz;  // Controlled_Buffer controlled_buffer_16
  assign rdMEM = rdMEM_t ? 1'b1 : 1'bz;  // Controlled_Buffer controlled_buffer_17

  // Other names for the same wires on the sheet: immed = ADDRBUS[0]; memdir = ADDRBUS[1]; memind = ADDRBUS[2];
  //   regdir = ADDRBUS[3]; preincr = ADDRBUS[4]; postdec = ADDRBUS[5]; regindpom = ADDRBUS[6]; CLK = in_2;
  //   FCBUS = in_3; HALT = INSTRUCBUS[0]; RTS = INSTRUCBUS[1]; RTI = INSTRUCBUS[2]; ASL = INSTRUCBUS[3];
  //   POPPSW = INSTRUCBUS[4]; PUSH = INSTRUCBUS[5]; POP = INSTRUCBUS[6]; BEQL = INSTRUCBUS[7]; BNEQ = INSTRUCBUS[8];
  //   BLEQU = INSTRUCBUS[9]; BLSS = INSTRUCBUS[10]; JLEQ = INSTRUCBUS[11]; LD = INSTRUCBUS[12]; ST = INSTRUCBUS[13];
  //   JADR = INSTRUCBUS[14]; TST = INSTRUCBUS[15]; XOR = INSTRUCBUS[16]; STRLEN = INSTRUCBUS[17];
  //   JMP = INSTRUCBUS[18]; JSR = INSTRUCBUS[19]; ADDR = PHASEFFBUS[1]; rst = in_1

  // Notes on the sheet:
  //   Operaciona jedinica
  //   Upravljacka jedinica
endmodule

module EXEC (
  input  in_1,
  input  in_2,
  input  in_3,
  input  MDR_ZERO,
  input  [3:0] PHASEFFBUS,
  input  [19:0] INSTRUCBUS,
  input  [6:0] ADDRBUS,
  input  [15:0] PSW,
  output [14:0] CMEMBUS,
  output [7:0] CFFBUS,
  output [20:0] CREGBUS,
  output [6:0] CPSW,
  output rdMEM,
  output wrMEM
);

  wire and_1_out, and_2_out, and_3_out, and_4_out, and_5_out, and_6_out, and_7_out, and_8_out, and_9_out,
       and_10_out, andALU, aslALU, brcnd, brMDR_ZERO, brnotbrorjump, brnotEXEC, brnotFCBUS, bropr, brorjump,
       brregdir, bruncnd, clA, clEXEC, clPSWSTART, decSP, incALU, incMAR, incSP, ldA, ldC, ldDWH, ldDWL, ldI,
       ldMAR, ldMDR, ldN, ldPC, ldST, ldV, ldZ, mp2_8b_1_p3, mxA0, mxA1, mxGPR0, mxMAR1, mxMAR2, mxMDR0,
       mxMDR1, mxMDR2, mxPC0, mxPC1, not_1_out, or_1_out, or_2_out, rdMEM_t, reg8_inc_ld_1_p5,
       reg8_inc_ld_1_p6, stINTR, wrGPR, wrMEM_t, xor_1_out, xorALU;
  wire [2:0] dc3_8_1_p9;
  wire [6:0] mp2_8b_1_p2, mp2_8b_1_p4;
  wire [7:0] reg8_inc_ld_1_p4;

  // DC3_8 dc3_8_1: pin names not known; wires that end beside it: bropr, brMDR_ZERO, brregdir, brnotbrorjump, brnotFCBUS, brnotEXEC, bruncnd, 1'b1, dc3_8_1_p9
  or or_1 (or_1_out, PSW[1], PSW[4]);
  xor xor_1 (xor_1_out, PSW[2], PSW[3]);
  not not_1 (not_1_out, in_1);
  or or_2 (or_2_out, xor_1_out, PSW[1]);
  // MP2_8b mp2_8b_1: pin names not known; wires that end beside it: bropr, {1'b0, mp2_8b_1_p2}, mp2_8b_1_p3, {1'b0, mp2_8b_1_p4}, 1'b1
  // REG8_INC_LD reg8_inc_ld_1: pin names not known; wires that end beside it: in_2, not_1_out, mp2_8b_1_p3, reg8_inc_ld_1_p4, reg8_inc_ld_1_p5, reg8_inc_ld_1_p6
  not not_2 (reg8_inc_ld_1_p6, reg8_inc_ld_1_p5);
  and and_1 (and_1_out, PSW[1], INSTRUCBUS[7]);
  and and_2 (and_2_out, ~PSW[1], INSTRUCBUS[8]);  // AND_Gate
  and and_3 (and_3_out, INSTRUCBUS[9], or_1_out);
  and and_4 (and_4_out, INSTRUCBUS[10], xor_1_out);
  and and_5 (and_5_out, INSTRUCBUS[11], or_2_out);
  KMOPR kmopr_1 (
    .HALT(INSTRUCBUS[0]), .RTS(INSTRUCBUS[1]), .RTI(INSTRUCBUS[2]), .ASL(INSTRUCBUS[3]),
    .POPPSW(INSTRUCBUS[4]), .PUSH(INSTRUCBUS[5]), .POP(INSTRUCBUS[6]), .BEQL(INSTRUCBUS[7]),
    .BNEQ(INSTRUCBUS[8]), .BLEQU(INSTRUCBUS[9]), .BLSS(INSTRUCBUS[10]), .Adr6__0(mp2_8b_1_p4),
    .JLEQ(INSTRUCBUS[11]), .JMP(INSTRUCBUS[18]), .JSR(INSTRUCBUS[19]), .LD(INSTRUCBUS[12]),
    .ST(INSTRUCBUS[13]), .JADR(INSTRUCBUS[14]), .TST(INSTRUCBUS[15]), .XOR(INSTRUCBUS[16]),
    .STRLEN(INSTRUCBUS[17]));
  ROM_128X46 rom_128x46_1 (
    .ADDR6__0(reg8_inc_ld_1_p4[6:0]), .CS(1'b1),
    .DOUT45__32({mp2_8b_1_p2, dc3_8_1_p9, clEXEC, stINTR, incALU, clA}),
    .DOUT31__0({xorALU, andALU, mxGPR0, wrGPR, incMAR, mxA1, mxMDR2, mxPC1, mxPC0, mxMDR0, wrMEM_t, mxMDR1, incSP, aslALU, mxA0, ldA, ldI, ldV, ldC, ldN, ldZ, ldST, ldPC, ldDWL, ldDWH, ldMDR, rdMEM_t, decSP, mxMAR2, mxMAR1, ldMAR, clPSWSTART}));
  or or_3 (reg8_inc_ld_1_p5, bropr, bruncnd, brcnd);
  or or_4 (brorjump, and_1_out, and_2_out, and_3_out, and_4_out, and_5_out);
  and and_6 (and_6_out, brnotbrorjump, ~brorjump);  // AND_Gate
  and and_7 (and_7_out, brregdir, ADDRBUS[3]);
  and and_8 (and_8_out, brMDR_ZERO, MDR_ZERO);
  and and_9 (and_9_out, brnotFCBUS, ~in_3);  // AND_Gate
  and and_10 (and_10_out, brnotEXEC, ~PHASEFFBUS[2]);  // AND_Gate
  or or_5 (brcnd, and_6_out, and_7_out, and_8_out, and_9_out, and_10_out);
  assign CMEMBUS[0] = ldMAR ? 1'b1 : 1'bz;  // Controlled_Buffer controlled_buffer_1
  assign CMEMBUS[1] = incMAR ? 1'b1 : 1'bz;  // Controlled_Buffer controlled_buffer_2
  assign CMEMBUS[2] = ldMDR ? 1'b1 : 1'bz;  // Controlled_Buffer controlled_buffer_3
  assign CMEMBUS[3] = ldPC ? 1'b1 : 1'bz;  // Controlled_Buffer controlled_buffer_4
  assign CMEMBUS[6] = mxMAR1 ? 1'b1 : 1'bz;  // Controlled_Buffer controlled_buffer_5
  assign CMEMBUS[7] = mxMAR2 ? 1'b1 : 1'bz;  // Controlled_Buffer controlled_buffer_6
  assign CMEMBUS[8] = incSP ? 1'b1 : 1'bz;  // Controlled_Buffer controlled_buffer_7
  assign CMEMBUS[9] = decSP ? 1'b1 : 1'bz;  // Controlled_Buffer controlled_buffer_8
  assign CMEMBUS[10] = mxPC0 ? 1'b1 : 1'bz;  // Controlled_Buffer controlled_buffer_9
  assign CMEMBUS[11] = mxPC1 ? 1'b1 : 1'bz;  // Controlled_Buffer controlled_buffer_10
  assign CMEMBUS[12] = mxMDR2 ? 1'b1 : 1'bz;  // Controlled_Buffer controlled_buffer_11
  assign CMEMBUS[13] = mxMDR1 ? 1'b1 : 1'bz;  // Controlled_Buffer controlled_buffer_12
  assign CMEMBUS[14] = mxMDR0 ? 1'b1 : 1'bz;  // Controlled_Buffer controlled_buffer_13
  assign CREGBUS[5] = wrGPR ? 1'b1 : 1'bz;  // Controlled_Buffer controlled_buffer_14
  assign CREGBUS[6] = ldDWH ? 1'b1 : 1'bz;  // Controlled_Buffer controlled_buffer_15
  assign CREGBUS[7] = ldDWL ? 1'b1 : 1'bz;  // Controlled_Buffer controlled_buffer_16
  assign CREGBUS[8] = ldA ? 1'b1 : 1'bz;  // Controlled_Buffer controlled_buffer_17
  assign CREGBUS[9] = mxA0 ? 1'b1 : 1'bz;  // Controlled_Buffer controlled_buffer_18
  assign CREGBUS[10] = mxA1 ? 1'b1 : 1'bz;  // Controlled_Buffer controlled_buffer_19
  assign CREGBUS[15] = clA ? 1'b1 : 1'bz;  // Controlled_Buffer controlled_buffer_20
  assign CREGBUS[16] = mxGPR0 ? 1'b1 : 1'bz;  // Controlled_Buffer controlled_buffer_21
  assign CREGBUS[17] = incALU ? 1'b1 : 1'bz;  // Controlled_Buffer controlled_buffer_22
  assign CREGBUS[18] = aslALU ? 1'b1 : 1'bz;  // Controlled_Buffer controlled_buffer_23
  assign CREGBUS[19] = andALU ? 1'b1 : 1'bz;  // Controlled_Buffer controlled_buffer_24
  assign CREGBUS[20] = xorALU ? 1'b1 : 1'bz;  // Controlled_Buffer controlled_buffer_25
  assign CFFBUS[5] = clEXEC ? 1'b1 : 1'bz;  // Controlled_Buffer controlled_buffer_26
  assign CFFBUS[6] = stINTR ? 1'b1 : 1'bz;  // Controlled_Buffer controlled_buffer_27
  assign CPSW[0] = clPSWSTART ? 1'b1 : 1'bz;  // Controlled_Buffer controlled_buffer_28
  assign CPSW[1] = ldST ? 1'b1 : 1'bz;  // Controlled_Buffer controlled_buffer_29
  assign CPSW[2] = ldZ ? 1'b1 : 1'bz;  // Controlled_Buffer controlled_buffer_30
  assign CPSW[3] = ldN ? 1'b1 : 1'bz;  // Controlled_Buffer controlled_buffer_31
  assign CPSW[4] = ldC ? 1'b1 : 1'bz;  // Controlled_Buffer controlled_buffer_32
  assign CPSW[5] = ldV ? 1'b1 : 1'bz;  // Controlled_Buffer controlled_buffer_33
  assign CPSW[6] = ldI ? 1'b1 : 1'bz;  // Controlled_Buffer controlled_buffer_34
  assign rdMEM = rdMEM_t ? 1'b1 : 1'bz;  // Controlled_Buffer controlled_buffer_35
  assign wrMEM = wrMEM_t ? 1'b1 : 1'bz;  // Controlled_Buffer controlled_buffer_36

  // Other names for the same wires on the sheet: immed = ADDRBUS[0]; memdir = ADDRBUS[1]; memind = ADDRBUS[2];
  //   regdir = ADDRBUS[3]; preincr = ADDRBUS[4]; postdec = ADDRBUS[5]; regindpom = ADDRBUS[6]; CLK = in_2;
  //   FCBUS = in_3; HALT = INSTRUCBUS[0]; RTS = INSTRUCBUS[1]; RTI = INSTRUCBUS[2]; ASL = INSTRUCBUS[3];
  //   POPPSW = INSTRUCBUS[4]; PUSH = INSTRUCBUS[5]; POP = INSTRUCBUS[6]; BEQL = INSTRUCBUS[7]; BNEQ = INSTRUCBUS[8];
  //   BLEQU = INSTRUCBUS[9]; BLSS = INSTRUCBUS[10]; JLEQ = INSTRUCBUS[11]; LD = INSTRUCBUS[12]; ST = INSTRUCBUS[13];
  //   JADR = INSTRUCBUS[14]; TST = INSTRUCBUS[15]; XOR = INSTRUCBUS[16]; STRLEN = INSTRUCBUS[17];
  //   JMP = INSTRUCBUS[18]; JSR = INSTRUCBUS[19]; EXEC = PHASEFFBUS[2]; PSWZ = PSW[1]; PSWN = PSW[2]; PSWV = PSW[3];
  //   PSWC = PSW[4]; rst = in_1

  // Notes on the sheet:
  //   Upravljacka jedinica
  //   Operaciona jedinica
endmodule

module INTR (
  input  in_1,
  input  in_2,
  input  in_3,
  input  [3:0] PHASEFFBUS,
  input  [19:0] INSTRUCBUS,
  input  [15:0] PSW,
  input  [7:0] intr,
  output [15:0] ADDIVTP,
  output [2:0] UEXT__0,
  output inta,
  output [14:0] CMEMBUS,
  output [7:0] CFFBUS,
  output [20:0] CREGBUS,
  output rdMEM,
  output wrMEM
);

  wire and_2_out, and_3_out, and_4_out, brcnd, brnotFCBUS, brnotINTR, brnotPREKID, bruncd, clINTR, incMAR,
       incSP, ldDWH, ldDWL, ldMAR, ldMDR, ldPC, mxMAR0, mxMAR1, mxMAR2, mxMDR0, mxMDR1, mxMDR2, not_1_out,
       not_3_out, or_1_out, PREKID, rdMEM_t, reg8_inc_ld_1_p5, reg8_inc_ld_1_p6, stFETCH, wrMEM_t;
  wire [2:0] reg8_inc_ld_1_p3;
  wire [3:1] IVTDSP15__0;
  wire [7:0] reg8_inc_ld_1_p4;
  wire [15:0] IVTP15__0;
  wire [25:18] dc3_8_1_p6;

  and and_1 (PREKID, or_1_out, PSW[15], ~INSTRUCBUS[0]);  // AND_Gate
  or or_1 (or_1_out, intr[7], intr[6], intr[5], intr[4], intr[3], intr[2], intr[1], intr[0]);
  not not_1 (not_1_out, in_1);
  // REG8_INC_LD reg8_inc_ld_1: pin names not known; wires that end beside it: in_2, not_1_out, {reg8_inc_ld_1_p3, dc3_8_1_p6[25:21]}, reg8_inc_ld_1_p4, reg8_inc_ld_1_p5, reg8_inc_ld_1_p6
  // DC3_8 dc3_8_1: pin names not known; wires that end beside it: brnotFCBUS, brnotPREKID, brnotINTR, bruncd, 1'b1, dc3_8_1_p6[20:18]
  not not_2 (reg8_inc_ld_1_p6, reg8_inc_ld_1_p5);
  or or_2 (reg8_inc_ld_1_p5, bruncd, brcnd);
  ROM_32X26 rom_32x26_1 (
    .ADDR4__0(reg8_inc_ld_1_p4[4:0]), .CS(1'b1),
    .DOUT({dc3_8_1_p6, clINTR, stFETCH, ldPC, ldDWH, incMAR, ldDWL, rdMEM_t, mxMAR0, inta, mxMDR1, mxMDR0, wrMEM_t, mxMDR2, ldMDR, mxMAR2, mxMAR1, ldMAR, incSP}));
  // CD8 cd8_1: pin names not known; wires that end beside it: intr[7], intr[6], intr[5], intr[4], intr[3], intr[2], intr[1], intr[0], 1'b1, UEXT__0[2], UEXT__0[1], UEXT__0[0]
  // REG3_LD reg3_ld_1: pin names not known; wires that end beside it: in_2, UEXT__0, IVTDSP15__0, inta
  not not_3 (not_3_out, in_1);
  // REG16_LD reg16_ld_1: pin names not known; wires that end beside it: in_2, not_3_out, IVTP15__0
  and and_2 (and_2_out, ~PHASEFFBUS[3], brnotINTR);  // AND_Gate
  and and_3 (and_3_out, ~in_3, brnotFCBUS);  // AND_Gate
  and and_4 (and_4_out, ~PREKID, brnotPREKID);  // AND_Gate
  // ADD16 add16_1: pin names not known; wires that end beside it: IVTP15__0, ADDIVTP, {{12{1'b0}}, IVTDSP15__0, 1'b0}, 1'b0
  or or_3 (brcnd, and_2_out, and_3_out, and_4_out);
  assign CMEMBUS[0] = ldMAR ? 1'b1 : 1'bz;  // Controlled_Buffer controlled_buffer_1
  assign CMEMBUS[1] = incMAR ? 1'b1 : 1'bz;  // Controlled_Buffer controlled_buffer_2
  assign CMEMBUS[2] = ldMDR ? 1'b1 : 1'bz;  // Controlled_Buffer controlled_buffer_3
  assign CMEMBUS[3] = ldPC ? 1'b1 : 1'bz;  // Controlled_Buffer controlled_buffer_4
  assign CMEMBUS[5] = mxMAR0 ? 1'b1 : 1'bz;  // Controlled_Buffer controlled_buffer_5
  assign CMEMBUS[6] = mxMAR1 ? 1'b1 : 1'bz;  // Controlled_Buffer controlled_buffer_6
  assign CMEMBUS[7] = mxMAR2 ? 1'b1 : 1'bz;  // Controlled_Buffer controlled_buffer_7
  assign CMEMBUS[8] = incSP ? 1'b1 : 1'bz;  // Controlled_Buffer controlled_buffer_8
  assign CMEMBUS[12] = mxMDR2 ? 1'b1 : 1'bz;  // Controlled_Buffer controlled_buffer_9
  assign CMEMBUS[13] = mxMDR1 ? 1'b1 : 1'bz;  // Controlled_Buffer controlled_buffer_10
  assign CMEMBUS[14] = mxMDR0 ? 1'b1 : 1'bz;  // Controlled_Buffer controlled_buffer_11
  assign CFFBUS[0] = stFETCH ? 1'b1 : 1'bz;  // Controlled_Buffer controlled_buffer_12
  assign CFFBUS[7] = clINTR ? 1'b1 : 1'bz;  // Controlled_Buffer controlled_buffer_13
  assign CREGBUS[6] = ldDWH ? 1'b1 : 1'bz;  // Controlled_Buffer controlled_buffer_14
  assign CREGBUS[7] = ldDWL ? 1'b1 : 1'bz;  // Controlled_Buffer controlled_buffer_15
  assign rdMEM = rdMEM_t ? 1'b1 : 1'bz;  // Controlled_Buffer controlled_buffer_16
  assign wrMEM = wrMEM_t ? 1'b1 : 1'bz;  // Controlled_Buffer controlled_buffer_17

  // Other names for the same wires on the sheet: ldBR = inta; ADDIVTP15__0[15:0] = ADDIVTP; CLK = in_2; FCBUS = in_3;
  //   HALT = INSTRUCBUS[0]; RTS = INSTRUCBUS[1]; RTI = INSTRUCBUS[2]; ASL = INSTRUCBUS[3]; POPPSW = INSTRUCBUS[4];
  //   PUSH = INSTRUCBUS[5]; POP = INSTRUCBUS[6]; BEQL = INSTRUCBUS[7]; BNEQ = INSTRUCBUS[8]; BLEQU = INSTRUCBUS[9];
  //   BLSS = INSTRUCBUS[10]; JLEQ = INSTRUCBUS[11]; LD = INSTRUCBUS[12]; ST = INSTRUCBUS[13]; JADR = INSTRUCBUS[14];
  //   TST = INSTRUCBUS[15]; XOR = INSTRUCBUS[16]; STRLEN = INSTRUCBUS[17]; JMP = INSTRUCBUS[18]; JSR = INSTRUCBUS[19];
  //   intr7__0[7:0] = intr; INTR_t = PHASEFFBUS[3]; PSWI = PSW[15]; rst = in_1; UEXT2__0[2:0] = UEXT__0

  // Notes on the sheet:
  //   Operaciona jedinica
  //   Upravljacka jedinica
endmodule

module RAM (
  input  [15:0] in_1,
  input  in_2,
  input  [7:0] in_3,
  input  in_4,
  input  in_5,
  input  in_6,
  output [7:0] out_7,
  output out_8
);

  wire and_1_out, and_2_out, CNT0, LDCNT, not_1_out, notCNT0, or_1_out, reg4_ld_sl_sr_1_p6, rsff_2_p4,
       rsff_2_p5, rsff_3_p4, sl;
  wire [3:0] CNT, LFSR;

  // RSFF rsff_1: pin names not known; wires that end beside it: 1'b0, in_2, in_6, sl
  or or_1 (or_1_out, in_4, in_5);
  // REG4_LD_SL_SR reg4_ld_sl_sr_1: pin names not known; wires that end beside it: 1'b0, 1'b0, in_2, 4'b1111, LFSR, reg4_ld_sl_sr_1_p6, sl, in_6
  // RisingEdge risingedge_1: pin names not known; wires that end beside it: or_1_out, in_2, LDCNT
  // MEM64Kx8 mem64kx8_1: pin names not known; wires that end beside it: in_1, 1'b1, in_2, in_3, out_7, in_4
  xor xor_1 (reg4_ld_sl_sr_1_p6, LFSR[2], LFSR[3]);
  and and_1 (and_1_out, CNT0, not_1_out);
  not not_1 (not_1_out, LDCNT);
  // RSFF rsff_2: pin names not known; wires that end beside it: and_1_out, in_2, LDCNT, rsff_2_p4, rsff_2_p5
  not not_2 (rsff_2_p4, in_6);
  and and_2 (and_2_out, rsff_2_p5, CNT0);
  // REG4m_DEC_LD reg4m_dec_ld_1: pin names not known; wires that end beside it: in_2, LFSR, CNT, LDCNT, notCNT0, notCNT0
  or or_2 (notCNT0, CNT[0], CNT[1], CNT[2], CNT[3]);
  // RSFF rsff_3: pin names not known; wires that end beside it: out_8, in_2, and_2_out, rsff_3_p4, out_8
  not not_3 (rsff_3_p4, in_6);
  not not_4 (CNT0, notCNT0);

  // Other names for the same wires on the sheet: ADR[15:0] = in_1; CLK = in_2; DIN[7:0] = in_3; DOUT[7:0] = out_7;
  //   fc = out_8; RDMEM = in_5; rst = in_6; WRMEM = in_4

  // Notes on the sheet:
  //   Random broj predstavlja vreme pristupa memoriji
  //   Brojac za generisanje random broja 
  //   Jedinica za generisanje function complete (fc) signala
  //   Brojac za dekrementiranje random broja
endmodule
